# Fritzing sketch Parking_Bar (saved by Fritzing 0.9.3b)
breadboards: 1

parts:
  J1 = Basic Servo
  HC-SR04_Sensor_1 = HC-SR04 Ultrasonic Distance Sensor
  부품1 = Arduino Uno (Rev3)
  HC-SR04_Sensor_2 = HC-SR04 Ultrasonic Distance Sensor

nets:
  GND: J1.gnd, HC-SR04_Sensor_1.GND, 부품1.GND, HC-SR04_Sensor_2.GND
  VCC: J1.vcc, HC-SR04_Sensor_1.VCC, 부품1.5V, HC-SR04_Sensor_2.VCC
  N1: J1.pulse, 부품1.D13/SCK
  N2: HC-SR04_Sensor_1.TRIG, 부품1.D7
  N3: HC-SR04_Sensor_1.ECHO, 부품1.D6_PWM
  N4: 부품1.D4, HC-SR04_Sensor_2.ECHO
  N5: 부품1.D5_PWM, HC-SR04_Sensor_2.TRIG
