# Fritzing sketch RC_Car (saved by Fritzing 0.9.3b)
breadboards: 1

parts:
  부품1 = Arduino Uno (Rev3)
  U1 = L9110 H-bridge module [part_number="L9110 H-bridge"]
  M1 = DC Motor
  M2 = DC Motor
  HC-SR04_Sensor_1 = HC-SR04 Ultrasonic Distance Sensor

nets:
  N1: 부품1.D10_PWM/SS, HC-SR04_Sensor_1.ECHO
  N2: 부품1.D11_PWM/MOSI, HC-SR04_Sensor_1.TRIG
  N3: 부품1.D4, U1.B-IB
  N4: 부품1.D5_PWM, U1.B-IA
  N5: 부품1.D6_PWM, U1.A-IA
  N6: 부품1.D7, U1.A-IB
  N7: U1.MOTOR_A-A, M2.pin_2
  N8: U1.MOTOR_A-B, M2.pin_1
  N9: U1.MOTOR_B-A, M1.pin_2
  N10: U1.MOTOR_B-B, M1.pin_1
