# Fritzing sketch RC_Car_sv (saved by Fritzing 0.9.3b)
breadboards: 1

parts:
  부품1 = Arduino Uno (Rev3)
  U1 = L9110 H-bridge module [part_number="L9110 H-bridge"]
  M1 = DC Motor
  M2 = DC Motor
  HC-SR04_Sensor_1 = HC-SR04 Ultrasonic Distance Sensor
  TCRT1 = TCRT5000 digital module [part_number=151608]
  TCRT2 = TCRT5000 digital module [part_number=151608]
  VCC1 = Battery block 9V
  VCC2 = Battery block 9V
  M3 = ESP-01 Adapter [part_number=ESP8266]

nets:
  N1: 부품1.D8, TCRT1.DO1
  N2: 부품1.D9_PWM, TCRT2.DO1
  N3: 부품1.D10_PWM/SS, HC-SR04_Sensor_1.ECHO
  N4: 부품1.D11_PWM/MOSI, HC-SR04_Sensor_1.TRIG
  N5: 부품1.D2, M3.RX
  N6: 부품1.D3_PWM, M3.TX
  N7: 부품1.D4, U1.B-IB
  N8: 부품1.D5_PWM, U1.B-IA
  N9: 부품1.D6_PWM, U1.A-IA
  N10: 부품1.D7, U1.A-IB
  VCC: 부품1.3V3, TCRT1.VCC, TCRT2.VCC
  VCC_2: 부품1.5V, HC-SR04_Sensor_1.VCC, M3.VCC
  GND: 부품1.GND, U1.GND, HC-SR04_Sensor_1.GND, TCRT1.GND, TCRT2.GND, VCC1.-, VCC2.-, M3.GND
  N11: 부품1.VIN, VCC2.+
  N12: U1.VCC, VCC1.+
  N13: U1.MOTOR_A-A, M2.pin_2
  N14: U1.MOTOR_A-B, M2.pin_1
  N15: U1.MOTOR_B-A, M1.pin_2
  N16: U1.MOTOR_B-B, M1.pin_1

custom parts:
  TCRT5000 digital module: breakout board for TCRT5000 module, convert analog to digital - Uses TCRT5000 infrared reflectance sensor - Detection distance: 1mm~8mm - Focus distance: 2.5mm - Working voltage: 3.3V~12V - Uses wide voltage LM393 comparator - With multi-turn precision potentiometer to adjust the sensitivity - Current: > 15mA - Output type: Digital switch output (0, 1) - Suitable for watt-hour meter pulse data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
  ESP-01 Adapter: Generic ESP-10 Adapter module with ESP8266 wireless module installed.
